# Fritzing sketch rori (saved by Fritzing 0.9.3b)

parts:
  U1 = NodeMCU V1.0
  M1 = ph-4502c [package=THT]
  U2 = DFRobot SEN0189 [package=THT]
  Part1 = Arduino Uno (Rev3)

nets:
  N1: U1.D1, Part1.D2
  N2: U1.D2, Part1.D3_PWM
  N3: M1.pin3, Part1.A1
  N4: M1.pin4, M1.pin5, U2.P1_3, Part1.GND
  N5: M1.pin6, Part1.5V
  N6: U2.P1_1, Part1.A0
  N7: U2.P1_2, Part1.3V3

custom parts:
  NodeMCU V1.0: ESP8266 based NodeMCU
  ph-4502c: ph-4502c PH Meter.
  DFRobot SEN0189: Turbidity sensor of DFRobot SEN0189
